# Fritzing sketch schematicFile (saved by Fritzing 0.9.4)
breadboards: 1

parts:
  Part1 = Arduino Uno (Rev3)
  IR1 = TSOP312.., 314.. [package=THT]
  D1 = LTE-302 [package=lte-302]
  Q1 = NPN-Transistor [package="TO92 [THT]"]
  R1 = Resistor [tolerance=±5% resistance=470 package="0603 [SMD]"]
  LED1 = smd LED [color="Red (633nm)" package="0603 [SMD]"]
  R2 = Resistor [tolerance=±5% resistance=220 package="0603 [SMD]"]
  J1 = Basic Servo

nets:
  N1: Part1.D9_PWM, J1.pulse
  N2: Part1.D13/SCK, R2.Pin_1
  N3: Part1.D2, IR1.Data
  N4: Part1.D3_PWM, R1.Pin_0
  5V: Part1.5V, IR1.Vs, D1.A, J1.vcc
  GND: Part1.GND, IR1.GND, Q1.E, LED1.cathode, J1.gnd
  N5: D1.C, Q1.B
  N6: Q1.C, R1.Pin_1
  N7: LED1.anode, R2.Pin_0
